# Fritzing sketch ATtiny13 Programmer (saved by Fritzing 0.9.4)
circuit board: 8.46667cm x 5.64444cm
breadboards: 1

parts:
  Part1 = Arduino Uno (Rev3)
  U1 = ATTINY13 [package=dip]

nets:
  N1: Part1.D10_PWM/SS, U1.PB5(NRES)
  N2: Part1.D11_PWM/MOSI, U1.PB0(MOSI)
  N3: Part1.D12/MISO, U1.PB1(MISO)
  N4: Part1.D13/SCK, U1.PB2(SCK_ADC1)
  5V: Part1.5V, U1.VCC
  GND: Part1.GND, U1.GND
